# Fritzing sketch Spannungsteiler (saved by Fritzing 0.9.3b)
breadboards: 1

parts:
  WeMos_D1_Mini1 = WeMos D1 Mini
  J1 = Screw terminal - 2 pins [package=THT]
  R1 = Resistor [tolerance=±5% resistance=1M package=THT]
  R2 = Resistor [tolerance=±5% resistance=147k package=THT]

nets:
  N1: WeMos_D1_Mini1.A0, R1.Pin_1, R2.Pin_1
  N2: WeMos_D1_Mini1.G, J1.pin1, R2.Pin_0
  N3: J1.pin2, R1.Pin_0
